// Logisim project D flip flop.circ as structural Verilog: 1 circuit, main circuit main
module main (
  input  S_prime,
  input  R_prime,
  input  D,
  input  CLK,
  output Q_prime,
  output Q,
  output Q_2,
  output Q_prime_2
);

  wire nand_1_out, nand_2_out, nand_3_out, nand_4_out, nand_5_out, nand_6_out, not_1_out, not_2_out;

  not not_1 (not_1_out, D);
  Clock clock_1 ();  // open: out
  nor nor_1 (Q_prime, S_prime, Q);
  nor nor_2 (Q, Q_prime, R_prime);
  nand nand_1 (nand_1_out, D, CLK);
  nand nand_2 (nand_2_out, not_1_out, CLK);
  not not_2 (not_2_out, CLK);
  nand nand_3 (nand_3_out, nand_1_out, nand_4_out);
  nand nand_4 (nand_4_out, nand_3_out, nand_2_out);
  nand nand_5 (nand_5_out, nand_3_out, not_2_out);
  nand nand_6 (nand_6_out, not_2_out, not_2_out, nand_4_out);
  nand nand_7 (Q_2, nand_5_out, Q_prime_2);
  nand nand_8 (Q_prime_2, Q_2, nand_6_out);
endmodule
