// Logisim project flip flop.circ as structural Verilog: 1 circuit, main circuit main
module main (
  input  S,
  input  R,
  input  S_2,
  input  R_2,
  output NQ,
  output Q,
  output NQ_2,
  output Q_2
);

  wire clock_1_out, nand_1_out, nand_2_out, t_ff_1_q, t_ff_1_qn;

  Clock clock_1 (.out(clock_1_out));
  nor nor_1 (NQ_2, S_2, Q_2);
  nor nor_2 (Q_2, NQ_2, R_2);
  nand nand_1 (nand_1_out, S, S);
  nand nand_2 (nand_2_out, R, R);
  LED led_1 (.in(t_ff_1_q));
  T_Flip_Flop t_ff_1 (.clk(clock_1_out), .T(1'b1), .Q(t_ff_1_q), .Qn(t_ff_1_qn));  // open: preset, reset, en
  LED led_2 (.in(t_ff_1_qn));
  nand nand_3 (NQ, nand_1_out, Q);
  nand nand_4 (Q, NQ, nand_2_out);
endmodule
